# Fritzing sketch DIGITAL (saved by Fritzing 0.9.3b)
circuit board: 7cm x 7cm
breadboards: 1

parts:
  J2 = female pin header, 2 pins [form="♀ (female)" part_number="VIN 12V"]
  U2 = Optocoupler [part_number=4N28 package=THT]
  J3 = female pin header, 2 pins [form="♀ (female)"]
  D6 = Diode [part_number=1N4148 package=diode-1n4148]
  R19 = Resistor [tolerance=±5% resistance=330 package=THT]
  R31 = Resistor [tolerance=±5% resistance=2.2k package=THT]
  Q15 = NPN-Transistor [part_number=BC548 package="TO92 [THT]"]
  Q16 = NPN-Transistor [part_number=BC548 package="TO92 [THT]"]
  R32 = Resistor [tolerance=±5% resistance=10k package=THT]
  R33 = Resistor [tolerance=±5% resistance=220 package=THT]
  R34 = Resistor [tolerance=±5% resistance=220 package=THT]
  J4 = female pin header, 2 pins [form="♀ (female)"]
  R35 = Resistor [tolerance=±5% resistance=10k package=THT]
  IC4 = IC, DIP package, 8 pins [chip_label=24LC256 part_number=24LC256]
  R72 = Resistor [tolerance=±5% resistance=220 package=THT]
  R73 = Resistor [tolerance=±5% resistance=10k package=THT]
  SUSTAIN_PEDAL_INPUT = female pin header, 2 pins [form="♀ (female)"]
  R76 = Resistor [tolerance=±5% resistance=10k package=THT]
  Q21 = NPN-Transistor [part_number=BC548 package="TO92 [THT]"]
  R77 = Resistor [tolerance=±5% resistance=10k package=THT]
  SYNC_IN = female pin header, 2 pins [form="♀ (female)"]
  R78 = Resistor [tolerance=±5% resistance=100k package=THT]
  Q22 = NPN-Transistor [part_number=BC548 package="TO92 [THT]"]
  R79 = Resistor [tolerance=±5% resistance=10k package=THT]
  R80 = Resistor [tolerance=±5% resistance=1k package=THT]
  SYNC_OUT = female pin header, 2 pins [form="♀ (female)"]
  OLED = female pin header, 7 pins [form="♀ (female)"]
  SDCARD = female pin header, 6 pins [form="♀ (female)"]
  R82 = Resistor [tolerance=±5% resistance=1k package=THT]
  R83 = Resistor [tolerance=±5% resistance=1k package=THT]
  IC1 = Voltage Regulator [part_number=7809 package=to220-igo]
  C21 = Ceramic Capacitor [capacitance=100nF package="200 mil [THT, multilayer]"]
  C22 = Electrolytic Capacitor [capacitance=0.1mF voltage=16V package="200 mil [THT, electrolytic]"]
  IC5 = Voltage Regulator [part_number=7805 package=to220-igo]
  C23 = Electrolytic Capacitor [capacitance=100µF voltage=16V package="100 mil [THT, electrolytic]"]
  C24 = Ceramic Capacitor [capacitance=100nF package="200 mil [THT, multilayer]"]
  J5 = female pin header, 3 pins [form="♀ (female)" part_number="TO VOICES PCB"]
  C25 = Ceramic Capacitor [capacitance=100nF package="200 mil [THT, multilayer]"]
  GND_FOR_ENCODERS = female pin header, 4 pins [form="♀ (female)"]
  J7 = female pin header, 2 pins [form="♀ (female)" part_number="TX/RX FROM DUE"]
  J8 = female pin header, 2 pins [form="♀ (female)" part_number="SDA/SCL FROM DUE"]
  SPI_TO_DUE = female pin header, 7 pins [form="♀ (female)"]
  C26 = Electrolytic Capacitor [capacitance=10µF package="100 mil [THT, electrolytic]"]
  D7 = Diode [part_number=1N4148 package=diode-1n4148]
  J9 = female pin header, 3 pins [form="♀ (female)" part_number="TO VCF PCB"]
  POWER_TO_DUE = female pin header, 6 pins [form="♀ (female)"]
  J10 = female pin header, 3 pins [form="♀ (female)"]
  IOs_TO_DUE = female pin header, 3 pins [form="♀ (female)"]
  GND_FOR_SWITCHES = female pin header, 8 pins [form="♀ (female)"]

nets:
  12V: J2.pin1, IC1.IN, C21.1, C22.+, IC5.IN, POWER_TO_DUE.pin6
  GND: J2.pin2, U2.Pin_4, Q15.E, Q16.E, IC4.pin1, IC4.pin2, IC4.pin3, IC4.pin4, IC4.pin7, SUSTAIN_PEDAL_INPUT.pin2, Q21.E, SYNC_IN.pin2, R78.Pin_1, Q22.E, SYNC_OUT.pin2, OLED.pin1, SDCARD.pin1, R83.Pin_0, IC1.GND, C21.0, C22.-, IC5.GND, C23.-, C24.0, J5.pin3, C25.0, GND_FOR_ENCODERS.pin1, GND_FOR_ENCODERS.pin2, GND_FOR_ENCODERS.pin3, GND_FOR_ENCODERS.pin4, C26.-, D7.A, J9.pin3, POWER_TO_DUE.pin4, POWER_TO_DUE.pin5, J10.pin3, GND_FOR_SWITCHES.pin1, GND_FOR_SWITCHES.pin2, GND_FOR_SWITCHES.pin3, GND_FOR_SWITCHES.pin4, GND_FOR_SWITCHES.pin5, GND_FOR_SWITCHES.pin6, GND_FOR_SWITCHES.pin7, GND_FOR_SWITCHES.pin8
  N1: U2.Pin_1, D6.C, R19.Pin_0
  N2: U2.Pin_2, J3.pin2, D6.A
  N3: U2.Pin_5, R31.Pin_0, J7.pin2
  N4: J3.pin1, R19.Pin_1
  3.3V: R31.Pin_1, IC4.pin8, R73.Pin_1, R76.Pin_1, OLED.pin2, C25.1, POWER_TO_DUE.pin2
  N5: Q15.B, R35.Pin_1
  N6: Q15.C, Q16.B, R32.Pin_0
  N7: Q16.C, R33.Pin_0
  5V: R32.Pin_1, R34.Pin_0, R80.Pin_1, SDCARD.pin2, IC5.OUT, C23.+, C24.1, J5.pin2, J9.pin2, J10.pin2
  N8: R33.Pin_1, J4.pin2
  N9: R34.Pin_1, J4.pin1
  N10: R35.Pin_0, J7.pin1
  N11: IC4.pin5, J8.pin2
  N12: IC4.pin6, J8.pin1
  N13: R72.Pin_0, IOs_TO_DUE.pin2
  N14: R72.Pin_1, R73.Pin_0, SUSTAIN_PEDAL_INPUT.pin1
  N15: R76.Pin_0, Q21.C, IOs_TO_DUE.pin3
  N16: Q21.B, R77.Pin_0, R78.Pin_0, D7.C
  N17: R77.Pin_1, SYNC_IN.pin1
  N18: Q22.B, R79.Pin_1
  N19: Q22.C, R80.Pin_0, SYNC_OUT.pin1
  N20: R79.Pin_0, IOs_TO_DUE.pin1
  CLK: OLED.pin3, SDCARD.pin5, SPI_TO_DUE.pin2
  MOSI: OLED.pin4, SDCARD.pin4, SPI_TO_DUE.pin1
  LCD_RES: OLED.pin5, SPI_TO_DUE.pin7
  LCD_DC: OLED.pin6, SPI_TO_DUE.pin6
  LCD_CS: OLED.pin7, SPI_TO_DUE.pin5
  N21: SDCARD.pin3, R82.Pin_1
  SD_CS: SDCARD.pin6, SPI_TO_DUE.pin4
  MISO: R82.Pin_0, R83.Pin_1, SPI_TO_DUE.pin3
  9V: IC1.OUT, J5.pin1, J9.pin1, J10.pin1
  N22: C26.+, POWER_TO_DUE.pin1

notes:
  MIDI IN
  CUTOFF
  MIDI OUT
